// Logisim project CPU.circ as structural Verilog: 12 circuits, main circuit main
module main (
  input  [9:0] in_1,
  input  Reset,
  input  B0,
  output [4:0] out_4
);

  wire CLK;
  wire [2:0] A_Sel, B, Decoder_Sel, undriven;
  wire [3:0] B_Sel;
  wire [4:0] OpCode;
  wire [6:0] WriteAddr;
  wire [9:0] ALU_Data, Data, multiplexer_1_out, multiplexer_2_out, R0, R1, R2, R3, R4, R5, R6;

  PC pc_1 (.CLK(CLK), .Write_Enable(1'b1), .Reset(Reset), .B0(1'b1), .B1_4(B0), .Data_Out(out_4));
  CLA Adder__How_Many_Bits ();  // open: A0, A1, A2, A3, A4, B0, B1, B2, B3, B4, Cin, out_12, Cout
  RAM #(.addrWidth(5), .dataWidth(24)) ram_1 (
    .addr(out_4), .data({OpCode, Decoder_Sel, A_Sel, B, Data}));  // open: sel, clk, ld, clr
  Decoder #(.select(3)) decoder_1 (
    .out0(WriteAddr[0]), .out1(WriteAddr[1]), .out2(WriteAddr[2]), .out3(WriteAddr[3]), .out4(WriteAddr[4]),
    .out5(WriteAddr[5]), .out6(WriteAddr[6]), .sel(Decoder_Sel));  // open: out7, en
  Multiplexer #(.select(3), .width(10), .enable("false")) multiplexer_1 (
    .in0(R0), .in1(R1), .in2(R2), .in3(R3), .in4(R4), .in5(R5), .in6(R6), .out(multiplexer_1_out), .sel(A_Sel));  // open: in7
  Multiplexer #(.select(4), .width(10), .enable("false")) multiplexer_2 (
    .in0(R0), .in1(R1), .in2(R2), .in3(R3), .in4(R4), .in5(R5), .in6(R6), .in7({10{1'b0}}), .in8(Data),
    .out(multiplexer_2_out), .sel(B_Sel));  // open: in9, in10, in11, in12, in13, in14, in15
  Clock clock_1 (.out(CLK));
  ALU alu_1 (.Select(undriven), .A(multiplexer_1_out), .B(multiplexer_2_out), .ALU_OUT(ALU_Data));
  Reg_Bank Register_Bank (
    .DataIn(ALU_Data), .CLK(CLK), .WriteAddr(WriteAddr), .R0(R0), .R1(R1), .R2(R2), .R3(R3), .R4(R4),
    .R5(R5), .R6(R6));
  // Pins of 3 and 4 bits meet at B_Sel

  // Notes on the sheet:
  //   From Control Unit
  //   Comes From Control Unit
endmodule

module ALU_temp (
  input  [2:0] Select,
  input  [9:0] A,
  input  [9:0] B,
  output [9:0] ALU_OUT
);

  wire AOut0, CLA_2_cout, CLA_cout;
  wire [4:0] CLA_out_12;
  wire [9:5] CLA_2_out_12;

  // BIT_ALU BIT_ALU_0: pin names not known; wires that end beside it: B[9], 1'b0, A[9], Select, AOut0
  CLA CLA (
    .A0(A[9]), .A1(A[8]), .A2(A[7]), .A3(A[6]), .A4(A[5]), .B0(B[9]), .B1(B[8]), .B2(B[7]), .B3(B[6]),
    .B4(B[5]), .out_12(CLA_out_12), .Cout(CLA_cout));  // open: Cin
  Multiplexer #(.select(3), .width(10), .enable("false")) multiplexer_1 (
    .out(ALU_OUT), .sel(Select));  // open: in0, in1, in2, in3, in4, in5, in6, in7
  CLA CLA_2 (
    .A0(A[4]), .A1(A[3]), .A2(A[2]), .A3(A[1]), .A4(A[0]), .B0(B[4]), .B1(B[3]), .B2(B[2]), .B3(B[1]),
    .B4(B[0]), .Cin(CLA_cout), .out_12(CLA_2_out_12), .Cout(CLA_2_cout));

  // Other names for the same wires on the sheet: A9 = A[0]; A8 = A[1]; A7 = A[2]; A6 = A[3]; A5 = A[4]; A4 = A[5];
  //   A3 = A[6]; A2 = A[7]; A1 = A[8]; A0 = A[9]; B9 = B[0]; B8 = B[1]; B7 = B[2]; B6 = B[3]; B5 = B[4]; B4 = B[5];
  //   B3 = B[6]; B2 = B[7]; B1 = B[8]; B0 = B[9]; SEL[2:0] = Select

  // Notes on the sheet:
  //   C10
endmodule

// ADD
module _1Bit_ADDER (
  input  A,
  input  B,
  input  CIN,
  output P,
  output S,
  output G
);

  wire and_2_out, or_1_out;

  xor xor_1 (P, A, B);
  and and_1 (G, A, B);
  xor xor_2 (S, P, CIN);
  and and_2 (and_2_out, P, CIN);
  or or_1 (or_1_out, and_2_out, G);

  // Notes on the sheet:
  //   Carry
endmodule

module CLA (
  input  A0,
  input  A1,
  input  A2,
  input  A3,
  input  A4,
  input  B0,
  input  B1,
  input  B2,
  input  B3,
  input  B4,
  input  Cin,
  output [4:0] out_12,
  output Cout
);

  wire ADD0_g, ADD0_p, ADD1_g, ADD1_p, ADD2_g, ADD2_p, ADD3_g, ADD3_p, ADD4_g, ADD4_p, CLA_BLOCK_c1,
       CLA_BLOCK_c2, CLA_BLOCK_c3, CLA_BLOCK_c4;

  _1Bit_ADDER ADD0 (.A(A0), .B(B0), .CIN(Cin), .P(ADD0_p), .S(out_12[0]), .G(ADD0_g));
  _1Bit_ADDER ADD1 (.A(A1), .B(B1), .CIN(CLA_BLOCK_c1), .P(ADD1_p), .S(out_12[1]), .G(ADD1_g));
  _1Bit_ADDER ADD2 (.A(A2), .B(B2), .CIN(CLA_BLOCK_c2), .P(ADD2_p), .S(out_12[2]), .G(ADD2_g));
  _1Bit_ADDER ADD3 (.A(A3), .B(B3), .CIN(CLA_BLOCK_c3), .P(ADD3_p), .S(out_12[3]), .G(ADD3_g));
  _1Bit_ADDER ADD4 (.A(A4), .B(B4), .CIN(CLA_BLOCK_c4), .P(ADD4_p), .S(out_12[4]), .G(ADD4_g));
  CLA_Block CLA_BLOCK (
    .C0(Cin), .P0(ADD0_p), .P1(ADD1_p), .P2(ADD2_p), .P3(ADD3_p), .P4(ADD4_p), .G0(ADD0_g), .G1(ADD1_g),
    .G2(ADD2_g), .G3(ADD3_g), .G4(ADD4_g), .C1(CLA_BLOCK_c1), .C2(CLA_BLOCK_c2), .C3(CLA_BLOCK_c3),
    .C4(CLA_BLOCK_c4), .C5(Cout));
endmodule

module CLA_Block (
  input  C0,
  input  P0,
  input  P1,
  input  P2,
  input  P3,
  input  P4,
  input  G0,
  input  G1,
  input  G2,
  input  G3,
  input  G4,
  output C1,
  output C2,
  output C3,
  output C4,
  output C5
);

  wire and_1_out, and_2_out, and_3_out, and_4_out, and_5_out, and_6_out, and_7_out, and_8_out, and_9_out,
       and_10_out, and_11_out, and_12_out, and_13_out, and_14_out, and_15_out;

  and and_1 (and_1_out, C0, P0);
  and and_2 (and_2_out, G0, P1);
  and and_3 (and_3_out, C0, P0, P1);
  and and_4 (and_4_out, G1, P2);
  and and_5 (and_5_out, G0, P1, P2);
  and and_6 (and_6_out, C0, P0, P1, P2);
  and and_7 (and_7_out, G2, P3);
  and and_8 (and_8_out, G1, P2, P3);
  and and_9 (and_9_out, G0, P1, P2, P3);
  and and_10 (and_10_out, C0, P0, P1, P2, P3);
  and and_11 (and_11_out, G3, P4);
  and and_12 (and_12_out, G2, P3, P4);
  and and_13 (and_13_out, G1, P2, P3, P4);
  and and_14 (and_14_out, G0, P1, P2, P3, P4);
  and and_15 (and_15_out, C0, P0, P1, P2, P3, P4);
  or or_1 (C1, G0, and_1_out);
  or or_2 (C2, G1, and_2_out, and_3_out);
  or or_3 (C3, G2, and_4_out, and_5_out, and_6_out);
  or or_4 (C4, G3, and_7_out, and_8_out, and_9_out, and_10_out);
  or or_5 (C5, G4, and_11_out, and_12_out, and_13_out, and_14_out, and_15_out);
endmodule

module _10bit_Register (
  input  CLK,
  input  WriteEnable,
  input  [9:0] Data_In,
  output [9:0] Data_out
);

  D_Flip_Flop d_ff_1 (.clk(CLK), .D(Data_In[0]), .Q(Data_out[0]), .en(WriteEnable));  // open: Qn, preset, reset
  D_Flip_Flop d_ff_2 (.clk(CLK), .D(Data_In[1]), .Q(Data_out[1]), .en(WriteEnable));  // open: Qn, preset, reset
  D_Flip_Flop d_ff_3 (.clk(CLK), .D(Data_In[2]), .Q(Data_out[2]), .en(WriteEnable));  // open: Qn, preset, reset
  D_Flip_Flop d_ff_4 (.clk(CLK), .D(Data_In[3]), .Q(Data_out[3]), .en(WriteEnable));  // open: Qn, preset, reset
  D_Flip_Flop d_ff_5 (.clk(CLK), .D(Data_In[4]), .Q(Data_out[4]), .en(WriteEnable));  // open: Qn, preset, reset
  D_Flip_Flop d_ff_6 (.clk(CLK), .D(Data_In[5]), .Q(Data_out[5]), .en(WriteEnable));  // open: Qn, preset, reset
  D_Flip_Flop d_ff_7 (.clk(CLK), .D(Data_In[6]), .Q(Data_out[6]), .en(WriteEnable));  // open: Qn, preset, reset
  D_Flip_Flop d_ff_8 (.clk(CLK), .D(Data_In[7]), .Q(Data_out[7]), .en(WriteEnable));  // open: Qn, preset, reset
  D_Flip_Flop d_ff_9 (.clk(CLK), .D(Data_In[8]), .Q(Data_out[8]), .en(WriteEnable));  // open: Qn, preset, reset
  D_Flip_Flop d_ff_10 (.clk(CLK), .D(Data_In[9]), .Q(Data_out[9]), .en(WriteEnable));  // open: Qn, preset, reset

  // Other names for the same wires on the sheet: Din0 = Data_In[0]; Din1 = Data_In[1]; Din2 = Data_In[2];
  //   Din3 = Data_In[3]; Din4 = Data_In[4]; Din5 = Data_In[5]; Din6 = Data_In[6]; Din7 = Data_In[7];
  //   Din8 = Data_In[8]; Din9 = Data_In[9]; D0 = Data_out[0]; D1 = Data_out[1]; D2 = Data_out[2]; D3 = Data_out[3];
  //   D4 = Data_out[4]; D5 = Data_out[5]; D6 = Data_out[6]; D7 = Data_out[7]; D8 = Data_out[8]; D9 = Data_out[9];
  //   WrEn = WriteEnable
endmodule

module Reg_Bank (
  input  [9:0] DataIn,
  input  [6:0] WriteAddr,
  input  CLK,
  output [9:0] R0,
  output [9:0] R1,
  output [9:0] R2,
  output [9:0] R3,
  output [9:0] R4,
  output [9:0] R5,
  output [9:0] R6
);

  _10bit_Register u_10bit_register_1 (.CLK(CLK), .Data_out(R0), .Data_In(DataIn), .WriteEnable(WriteAddr[0]));
  _10bit_Register u_10bit_register_2 (.CLK(CLK), .Data_out(R1), .Data_In(DataIn), .WriteEnable(WriteAddr[1]));
  _10bit_Register u_10bit_register_3 (.CLK(CLK), .Data_out(R2), .Data_In(DataIn), .WriteEnable(WriteAddr[2]));
  _10bit_Register u_10bit_register_4 (.CLK(CLK), .Data_out(R3), .Data_In(DataIn), .WriteEnable(WriteAddr[3]));
  _10bit_Register u_10bit_register_5 (.CLK(CLK), .Data_out(R4), .Data_In(DataIn), .WriteEnable(WriteAddr[4]));
  _10bit_Register u_10bit_register_6 (.CLK(CLK), .Data_out(R5), .Data_In(DataIn), .WriteEnable(WriteAddr[5]));
  _10bit_Register u_10bit_register_7 (.CLK(CLK), .Data_out(R6), .Data_In(DataIn), .WriteEnable(WriteAddr[6]));

  // Notes on the sheet:
  //   R0
  //   R1
  //   R2
  //   R3
  //   R4
  //   R5
  //   R6
endmodule

module BIT_ALU (
  input  in_1,
  input  in_2,
  input  in_3,
  input  in_4,
  input  in_5,
  input  [2:0] in_6,
  output ALU_OUT,
  output Pout,
  output Gout
);

  wire and_1_out, n1bit_adder_1_s, not_1_out, or_1_out;

  and and_1 (and_1_out, in_1, in_2);
  or or_1 (or_1_out, in_1, in_2);
  not not_1 (not_1_out, in_1);
  _1Bit_ADDER u_1bit_adder_1 (.A(in_1), .B(in_2), .CIN(in_3), .P(Pout), .S(n1bit_adder_1_s), .G(Gout));
  Multiplexer #(.select(3), .enable("false")) multiplexer_1 (
    .in0(and_1_out), .in1(or_1_out), .in2(not_1_out), .in3(n1bit_adder_1_s), .in4(in_1), .in5(in_4),
    .in6(in_5), .out(ALU_OUT), .sel(in_6));  // open: in7

  // Other names for the same wires on the sheet: An = in_1; An_1 = in_5; An_1_t = in_4; Bn = in_2; CIN = in_3;
  //   SEL[2:0] = in_6

  // Notes on the sheet:
  //   AND
  //   OR
  //   MOVE
  //   NOT
endmodule

module ALU (
  input  [2:0] Select,
  input  [9:0] A,
  input  [9:0] B,
  output [9:0] ALU_OUT
);

  wire C0, C1, C2, C3, C4, C5, C6, C7, C8, C9, C10, G0, G1, G2, G3, G4, G5, G6, G7, G8, G9, P0, P1, P2, P3,
       P4, P5, P6, P7, P8, P9;

  BIT_ALU BIT_ALU_0 (
    .in_1(A[0]), .in_2(B[0]), .in_3(C0), .in_4(1'b0), .in_5(A[1]), .in_6(Select), .ALU_OUT(ALU_OUT[0]),
    .Pout(P0), .Gout(G0));
  BIT_ALU BIT_ALU_1 (
    .in_1(A[1]), .in_2(B[1]), .in_3(C1), .in_4(A[0]), .in_5(A[2]), .in_6(Select), .ALU_OUT(ALU_OUT[1]),
    .Pout(P1), .Gout(G1));
  BIT_ALU BIT_ALU_2 (
    .in_1(A[2]), .in_2(B[2]), .in_3(C2), .in_4(A[1]), .in_5(A[3]), .in_6(Select), .ALU_OUT(ALU_OUT[2]),
    .Pout(P2), .Gout(G2));
  BIT_ALU BIT_ALU_3 (
    .in_1(A[3]), .in_2(B[3]), .in_3(C3), .in_4(A[2]), .in_5(A[4]), .in_6(Select), .ALU_OUT(ALU_OUT[3]),
    .Pout(P3), .Gout(G3));
  BIT_ALU BIT_ALU_4 (
    .in_1(A[4]), .in_2(B[4]), .in_3(C4), .in_4(A[3]), .in_5(A[5]), .in_6(Select), .ALU_OUT(ALU_OUT[4]),
    .Pout(P4), .Gout(G4));
  CLA_Block cla_block_1 (
    .C0(C0), .P0(P0), .P1(P1), .P2(P2), .P3(P3), .P4(P4), .G0(G0), .G1(G1), .G2(G2), .G3(G3), .G4(G4),
    .C1(C1), .C2(C2), .C3(C3), .C4(C4), .C5(C5));
  BIT_ALU BIT_ALU_5 (
    .in_1(A[5]), .in_2(B[5]), .in_3(C5), .in_4(A[4]), .in_5(A[6]), .in_6(Select), .ALU_OUT(ALU_OUT[5]),
    .Pout(P5), .Gout(G5));
  BIT_ALU BIT_ALU_6 (
    .in_1(A[6]), .in_2(B[6]), .in_3(C6), .in_4(A[5]), .in_5(A[7]), .in_6(Select), .ALU_OUT(ALU_OUT[6]),
    .Pout(P6), .Gout(G6));
  CLA_Block cla_block_2 (
    .C0(C5), .P0(P5), .P1(P6), .P2(P7), .P3(P8), .P4(P9), .G0(G5), .G1(G6), .G2(G7), .G3(G8), .G4(G9),
    .C1(C6), .C2(C7), .C3(C8), .C4(C9), .C5(C10));
  BIT_ALU BIT_ALU_7 (
    .in_1(A[7]), .in_2(B[7]), .in_3(C7), .in_4(A[6]), .in_5(A[8]), .in_6(Select), .ALU_OUT(ALU_OUT[7]),
    .Pout(P7), .Gout(G7));
  BIT_ALU BIT_ALU_8 (
    .in_1(A[8]), .in_2(B[8]), .in_3(C8), .in_4(A[7]), .in_5(A[9]), .in_6(Select), .ALU_OUT(ALU_OUT[8]),
    .Pout(P8), .Gout(G8));
  BIT_ALU BIT_ALU_9 (
    .in_1(A[9]), .in_2(B[9]), .in_3(C9), .in_4(A[8]), .in_5(1'b0), .in_6(Select), .ALU_OUT(ALU_OUT[9]),
    .Pout(P9), .Gout(G9));

  // Other names for the same wires on the sheet: ALUOut0 = ALU_OUT[0]; ALUOut1 = ALU_OUT[1]; ALUOut2 = ALU_OUT[2];
  //   ALUOut3 = ALU_OUT[3]; ALUOut4 = ALU_OUT[4]; ALUOut5 = ALU_OUT[5]; ALUOut6 = ALU_OUT[6]; ALUOut7 = ALU_OUT[7];
  //   ALUOut8 = ALU_OUT[8]; ALUOut9 = ALU_OUT[9]; SEL[2:0] = Select
endmodule

module PC (
  input  CLK,
  input  Write_Enable,
  input  Reset,
  input  B0,
  input  B1_4,
  output [4:0] Data_Out
);

  wire [4:0] increment;

  _5bit_reg u_5bit_reg_1 (
    .CLK(CLK), .WriteEnable(Write_Enable), .Reset(Reset), .Data_In(increment), .Data_out(Data_Out));
  CLA cla_1 (
    .A0(Data_Out[0]), .A1(Data_Out[1]), .A2(Data_Out[2]), .A3(Data_Out[3]), .A4(Data_Out[4]), .B0(B0),
    .B1(B1_4), .B2(B1_4), .B3(B1_4), .B4(B1_4), .Cin(B1_4), .out_12(increment));  // open: Cout
endmodule

module PC_Adder (
  input  A,
  input  B,
  input  CIN,
  output P,
  output S,
  output G,
  output Cout
);

  wire and_2_out;

  xor xor_1 (P, A, B);
  and and_1 (G, A, B);
  xor xor_2 (S, P, CIN);
  and and_2 (and_2_out, P, CIN);
  or or_1 (Cout, and_2_out, G);
endmodule

module _5bit_reg (
  input  CLK,
  input  WriteEnable,
  input  Reset,
  input  [4:0] Data_In,
  output [4:0] Data_out
);

  D_Flip_Flop d_ff_1 (.clk(CLK), .D(Data_In[0]), .Q(Data_out[0]), .en(WriteEnable), .reset(Reset));  // open: Qn, preset
  D_Flip_Flop d_ff_2 (.clk(CLK), .D(Data_In[1]), .Q(Data_out[1]), .en(WriteEnable), .reset(Reset));  // open: Qn, preset
  D_Flip_Flop d_ff_3 (.clk(CLK), .D(Data_In[2]), .Q(Data_out[2]), .en(WriteEnable), .reset(Reset));  // open: Qn, preset
  D_Flip_Flop d_ff_4 (.clk(CLK), .D(Data_In[3]), .Q(Data_out[3]), .en(WriteEnable), .reset(Reset));  // open: Qn, preset
  D_Flip_Flop d_ff_5 (.clk(CLK), .D(Data_In[4]), .Q(Data_out[4]), .en(WriteEnable), .reset(Reset));  // open: Qn, preset

  // Other names for the same wires on the sheet: Din0 = Data_In[0]; Din1 = Data_In[1]; Din2 = Data_In[2];
  //   Din3 = Data_In[3]; Din4 = Data_In[4]; D0 = Data_out[0]; D1 = Data_out[1]; D2 = Data_out[2]; D3 = Data_out[3];
  //   D4 = Data_out[4]; WrEn = WriteEnable
endmodule
